// Logisim project cpu.circ as structural Verilog: 13 circuits, main circuit main
module main (
  input  reset
);

  wire add, addi, ALU_in_B, and_1_out, and_2_out, clk, eqz, inpu, is0, isLT, j, jal, jr, keyboard_1_avail,
       loadw, lt, memory_latch_1_oe_latched, memory_latch_1_we_latched, no, not_1_out, not_2_out, not_3_out,
       or_1_out, or_3_out, outpu, Rwe, savew, sl, sr, sub, xo;
  wire [2:0] multiplexer_2_out, rd, rs, rt, shamt, writeTo;
  wire [3:0] op;
  wire [5:0] instrucsplitter_1_imm;
  wire [7:0] keyInp;
  wire [11:0] address;
  wire [15:0] addandsub_2_result, ALU_Inp_2, ALU_out, bit_extender_1_out, data, dataOut, dOut, imm,
       memory_latch_1_address_latched, memory_latch_1_data_in_latched, multiplexer_4_out, multiplexer_5_out,
       multiplexer_6_out, multiplexer_8_out, PC_plus_one, qs, qt, RegFileInp, rom_1_data;

  Clock clock_1 (.out(clk));
  not not_1 (not_1_out, clk);
  not not_2 (not_2_out, clk);
  ROM #(.addrWidth(16), .dataWidth(16)) rom_1 (.addr(dOut), .data(rom_1_data));
  addAndSub addandsub_1 (.sub(1'b0), .A(16'h1), .B(dOut), .result(PC_plus_one));  // open: ovf
  RegisterFile registerfile_1 (
    .clk(clk), .rwe(Rwe), .reset(reset), .WriteData(RegFileInp), .ReadReg1(rs), .ReadReg2(rt), .rd(writeTo),
    .Reg1Contents(qs), .Reg2Contents(qt));
  ALU alu_1 (
    .inputData1(qs), .inputData2(ALU_Inp_2), .opType(op), .shamt(shamt), .outputData(ALU_out),
    .smaller(isLT), .allZeroes(is0));
  memory_latch memory_latch_1 (
    .address(ALU_out), .WE(savew), .clk(not_1_out), .data_in(qt),
    .address_latched(memory_latch_1_address_latched), .WE_latched(memory_latch_1_we_latched),
    .OE_latched(memory_latch_1_oe_latched), .data_in_latched(memory_latch_1_data_in_latched));
  PCReg pcreg_1 (.dataIn(data), .clk(not_2_out), .reset(reset), .dataOut(dOut));
  RAM #(.addrWidth(16), .dataWidth(16), .trigger("high"), .databus("bibus")) ram_1 (
    .addr(memory_latch_1_address_latched), .we(memory_latch_1_we_latched), .oe(memory_latch_1_oe_latched),
    .din(memory_latch_1_data_in_latched), .dout(dataOut));
  Multiplexer #(.width(16), .enable("false")) multiplexer_1 (.in0(qt), .in1(imm), .out(ALU_Inp_2), .sel(ALU_in_B));
  Multiplexer #(.width(3), .enable("false")) multiplexer_2 (
    .in0(rd), .in1(rt), .out(multiplexer_2_out), .sel(ALU_in_B));
  Multiplexer #(.width(3), .enable("false")) multiplexer_3 (
    .in0(multiplexer_2_out), .in1(3'b111), .out(writeTo), .sel(jal));
  addAndSub addandsub_2 (.sub(1'b0), .A(imm), .B(PC_plus_one), .result(addandsub_2_result));  // open: ovf
  and and_1 (and_1_out, eqz, is0);
  Multiplexer #(.width(16), .enable("false")) multiplexer_4 (
    .in0(ALU_out), .in1(dataOut), .out(multiplexer_4_out), .sel(loadw));
  Multiplexer #(.width(16), .enable("false")) multiplexer_5 (
    .in0(PC_plus_one), .in1(addandsub_2_result), .out(multiplexer_5_out), .sel(or_1_out));
  or or_1 (or_1_out, and_1_out, and_2_out);
  and and_2 (and_2_out, lt, isLT);
  InstrucSplitter instrucsplitter_1 (
    .Instruction(rom_1_data), .imm(instrucsplitter_1_imm), .Opcode(op), .rs(rs), .rt(rt), .rd(rd),
    .address(address), .shamt(shamt));
  Multiplexer #(.width(16), .enable("false")) multiplexer_6 (
    .in0(multiplexer_4_out), .in1(PC_plus_one), .out(multiplexer_6_out), .sel(jal));
  Decoder #(.select(4), .enable("false")) decoder_1 (
    .out0(add), .out1(sub), .out2(addi), .out3(no), .out4(xo), .out5(sl), .out6(sr), .out7(loadw),
    .out8(savew), .out9(eqz), .out10(lt), .out11(j), .out12(jr), .out13(jal), .out14(inpu), .out15(outpu),
    .sel(op));
  assign bit_extender_1_out = {{4{1'b0}}, address};  // Bit_Extender bit_extender_1
  Multiplexer #(.width(16), .enable("false")) multiplexer_7 (
    .in0(multiplexer_6_out), .in1({{8{1'b0}}, keyInp}), .out(RegFileInp), .sel(inpu));
  or or_2 (ALU_in_B, addi, savew, loadw);
  Multiplexer #(.width(16), .enable("false")) multiplexer_8 (
    .in0(multiplexer_5_out), .in1(bit_extender_1_out), .out(multiplexer_8_out), .sel(or_3_out));
  or or_3 (or_3_out, j, jal);
  assign imm = {{10{instrucsplitter_1_imm[5]}}, instrucsplitter_1_imm};  // Bit_Extender bit_extender_2
  Multiplexer #(.width(16), .enable("false")) multiplexer_9 (.in0(multiplexer_8_out), .in1(qs), .out(data), .sel(jr));
  or or_4 (Rwe, add, sub, xo, addi, no, sl, sr, loadw, jal, inpu);
  TTY #(.rows(13), .cols(80)) tty_1 (.data(qs[6:0]), .clk(clk), .we(outpu));  // open: clr
  not not_3 (not_3_out, clk);
  Keyboard keyboard_1 (.clk(not_3_out), .re(inpu), .clr(reset), .avail(keyboard_1_avail), .data(keyInp[6:0]));
  not not_4 (keyInp[7], keyboard_1_avail);

  // Other names for the same wires on the sheet: Rdst = ALU_in_B; rst = reset

  // Notes on the sheet:
  //   contents of rom_1 (hex, n*v repeats v):
  //   204b 208c 20cc 210d 2141 a446 2142 a4c6 2143 a506 2197 903f 219e 903f 219f 903f 207f 2144 a282 2198
  //   903f 2145 2041 9212 2146 2040 9202 2199 903f 2147 b021 219a 903f 2148 d025 214a 903f 2242 2149 ce00
  //   219b 903f 219c 903f
endmodule

module singleRegister (
  input  [15:0] datain,
  input  clk,
  input  writeEnable,
  input  reset,
  output [15:0] dataOut
);

  wire clk_t;

  and and_1 (clk_t, clk, writeEnable);
  D_Flip_Flop d_ff_1 (.D(datain[0]), .clk(clk_t), .Q(dataOut[0]), .reset(reset));  // open: Qn, preset
  D_Flip_Flop d_ff_2 (.D(datain[1]), .clk(clk_t), .Q(dataOut[1]), .reset(reset));  // open: Qn, preset
  D_Flip_Flop d_ff_3 (.D(datain[2]), .clk(clk_t), .Q(dataOut[2]), .reset(reset));  // open: Qn, preset
  D_Flip_Flop d_ff_4 (.D(datain[3]), .clk(clk_t), .Q(dataOut[3]), .reset(reset));  // open: Qn, preset
  D_Flip_Flop d_ff_5 (.D(datain[4]), .clk(clk_t), .Q(dataOut[4]), .reset(reset));  // open: Qn, preset
  D_Flip_Flop d_ff_6 (.D(datain[5]), .clk(clk_t), .Q(dataOut[5]), .reset(reset));  // open: Qn, preset
  D_Flip_Flop d_ff_7 (.D(datain[6]), .clk(clk_t), .Q(dataOut[6]), .reset(reset));  // open: Qn, preset
  D_Flip_Flop d_ff_8 (.D(datain[7]), .clk(clk_t), .Q(dataOut[7]), .reset(reset));  // open: Qn, preset
  D_Flip_Flop d_ff_9 (.D(datain[8]), .clk(clk_t), .Q(dataOut[8]), .reset(reset));  // open: Qn, preset
  D_Flip_Flop d_ff_10 (.D(datain[9]), .clk(clk_t), .Q(dataOut[9]), .reset(reset));  // open: Qn, preset
  D_Flip_Flop d_ff_11 (.D(datain[10]), .clk(clk_t), .Q(dataOut[10]), .reset(reset));  // open: Qn, preset
  D_Flip_Flop d_ff_12 (.D(datain[11]), .clk(clk_t), .Q(dataOut[11]), .reset(reset));  // open: Qn, preset
  D_Flip_Flop d_ff_13 (.D(datain[12]), .clk(clk_t), .Q(dataOut[12]), .reset(reset));  // open: Qn, preset
  D_Flip_Flop d_ff_14 (.D(datain[13]), .clk(clk_t), .Q(dataOut[13]), .reset(reset));  // open: Qn, preset
  D_Flip_Flop d_ff_15 (.D(datain[14]), .clk(clk_t), .Q(dataOut[14]), .reset(reset));  // open: Qn, preset
  D_Flip_Flop d_ff_16 (.D(datain[15]), .clk(clk_t), .Q(dataOut[15]), .reset(reset));  // open: Qn, preset

  // Other names for the same wires on the sheet: d0 = datain[0]; d1 = datain[1]; d2 = datain[2]; d3 = datain[3];
  //   d4 = datain[4]; d5 = datain[5]; d6 = datain[6]; d7 = datain[7]; d8 = datain[8]; d9 = datain[9];
  //   d10 = datain[10]; d11 = datain[11]; d12 = datain[12]; d13 = datain[13]; d14 = datain[14]; d15 = datain[15];
  //   o0 = dataOut[0]; o1 = dataOut[1]; o2 = dataOut[2]; o3 = dataOut[3]; o4 = dataOut[4]; o5 = dataOut[5];
  //   o6 = dataOut[6]; o7 = dataOut[7]; o8 = dataOut[8]; o9 = dataOut[9]; o10 = dataOut[10]; o11 = dataOut[11];
  //   o12 = dataOut[12]; o13 = dataOut[13]; o14 = dataOut[14]; o15 = dataOut[15]
endmodule

module RegisterFile (
  input  clk,
  input  rwe,
  input  reset,
  input  [15:0] WriteData,
  input  [2:0] ReadReg1,
  input  [2:0] ReadReg2,
  input  [2:0] rd,
  output [15:0] Reg1Contents,
  output [15:0] Reg2Contents
);

  wire clk_t, R1_0, R1_1, R1_2, R1_3, R1_4, R1_5, R1_6, R1_7, R2_0, R2_1, R2_2, R2_3, R2_4, R2_5, R2_6, R2_7,
       WE1, WE2, WE3, WE4, WE5, WE6, WE7;
  wire [15:0] singleregister_1_dataout, singleregister_2_dataout, singleregister_3_dataout,
       singleregister_4_dataout, singleregister_5_dataout, singleregister_6_dataout, singleregister_7_dataout;

  Decoder #(.select(3), .enable("false")) decoder_1 (
    .out0(R1_0), .out1(R1_1), .out2(R1_2), .out3(R1_3), .out4(R1_4), .out5(R1_5), .out6(R1_6), .out7(R1_7),
    .sel(ReadReg1));
  and and_1 (clk_t, clk, rwe);
  // Probe on {16{1'b0}}
  assign Reg1Contents = R1_0 ? {16{1'b0}} : 16'bz;  // Controlled_Buffer controlled_buffer_1
  assign Reg2Contents = R2_0 ? {16{1'b0}} : 16'bz;  // Controlled_Buffer controlled_buffer_2
  singleRegister singleregister_1 (
    .datain(WriteData), .clk(clk_t), .writeEnable(WE1), .reset(reset), .dataOut(singleregister_1_dataout));
  singleRegister singleregister_2 (
    .datain(WriteData), .clk(clk_t), .writeEnable(WE2), .reset(reset), .dataOut(singleregister_2_dataout));
  singleRegister singleregister_3 (
    .datain(WriteData), .clk(clk_t), .writeEnable(WE3), .reset(reset), .dataOut(singleregister_3_dataout));
  singleRegister singleregister_4 (
    .datain(WriteData), .clk(clk_t), .writeEnable(WE4), .reset(reset), .dataOut(singleregister_4_dataout));
  singleRegister singleregister_5 (
    .datain(WriteData), .clk(clk_t), .writeEnable(WE5), .reset(reset), .dataOut(singleregister_5_dataout));
  singleRegister singleregister_6 (
    .datain(WriteData), .clk(clk_t), .writeEnable(WE6), .reset(reset), .dataOut(singleregister_6_dataout));
  singleRegister singleregister_7 (
    .datain(WriteData), .clk(clk_t), .writeEnable(WE7), .reset(reset), .dataOut(singleregister_7_dataout));
  Decoder #(.select(3), .enable("false")) decoder_2 (
    .out0(R2_0), .out1(R2_1), .out2(R2_2), .out3(R2_3), .out4(R2_4), .out5(R2_5), .out6(R2_6), .out7(R2_7),
    .sel(ReadReg2));
  // Probe on singleregister_1_dataout
  // Probe on singleregister_2_dataout
  // Probe on singleregister_3_dataout
  // Probe on singleregister_4_dataout
  // Probe on singleregister_5_dataout
  // Probe on singleregister_6_dataout
  // Probe on singleregister_7_dataout
  assign Reg1Contents = R1_1 ? singleregister_1_dataout : 16'bz;  // Controlled_Buffer controlled_buffer_3
  assign Reg2Contents = R2_1 ? singleregister_1_dataout : 16'bz;  // Controlled_Buffer controlled_buffer_4
  assign Reg1Contents = R1_2 ? singleregister_2_dataout : 16'bz;  // Controlled_Buffer controlled_buffer_5
  assign Reg2Contents = R2_2 ? singleregister_2_dataout : 16'bz;  // Controlled_Buffer controlled_buffer_6
  assign Reg1Contents = R1_3 ? singleregister_3_dataout : 16'bz;  // Controlled_Buffer controlled_buffer_7
  assign Reg2Contents = R2_3 ? singleregister_3_dataout : 16'bz;  // Controlled_Buffer controlled_buffer_8
  assign Reg1Contents = R1_4 ? singleregister_4_dataout : 16'bz;  // Controlled_Buffer controlled_buffer_9
  assign Reg2Contents = R2_4 ? singleregister_4_dataout : 16'bz;  // Controlled_Buffer controlled_buffer_10
  assign Reg1Contents = R1_5 ? singleregister_5_dataout : 16'bz;  // Controlled_Buffer controlled_buffer_11
  assign Reg2Contents = R2_5 ? singleregister_5_dataout : 16'bz;  // Controlled_Buffer controlled_buffer_12
  assign Reg1Contents = R1_6 ? singleregister_6_dataout : 16'bz;  // Controlled_Buffer controlled_buffer_13
  assign Reg2Contents = R2_6 ? singleregister_6_dataout : 16'bz;  // Controlled_Buffer controlled_buffer_14
  assign Reg1Contents = R1_7 ? singleregister_7_dataout : 16'bz;  // Controlled_Buffer controlled_buffer_15
  assign Reg2Contents = R2_7 ? singleregister_7_dataout : 16'bz;  // Controlled_Buffer controlled_buffer_16
  Decoder #(.select(3), .enable("false")) decoder_3 (
    .out1(WE1), .out2(WE2), .out3(WE3), .out4(WE4), .out5(WE5), .out6(WE6), .out7(WE7), .sel(rd));  // open: out0

  // Other names for the same wires on the sheet: C1[15:0] = Reg1Contents; C2[15:0] = Reg2Contents
endmodule

module ALU (
  input  [15:0] inputData1,
  input  [15:0] inputData2,
  input  [3:0] opType,
  input  [2:0] shamt,
  output [15:0] outputData,
  output smaller,
  output allZeroes
);

  wire [15:0] addandsub_1_result, addandsub_2_result, addandsub_3_result, leftshift_1_result, not_1_out,
       rightshift_1_result, xor_1_out;

  assign not_1_out = ~inputData1;  // NOT_Gate not_1, 16 bits wide
  assign xor_1_out = inputData1 ^ inputData2;  // XOR_Gate xor_1, 16 bits wide
  addAndSub addandsub_1 (.sub(1'b0), .A(inputData1), .B(inputData2), .result(addandsub_1_result));  // open: ovf
  addAndSub addandsub_2 (.sub(1'b1), .A(inputData1), .B(inputData2), .result(addandsub_2_result));  // open: ovf
  addAndSub addandsub_3 (.sub(1'b0), .A(inputData1), .B(inputData2), .result(addandsub_3_result));  // open: ovf
  leftShift leftshift_1 (.A(inputData1), .shamt(shamt), .result(leftshift_1_result));
  rightShift rightshift_1 (.A(inputData1), .shamt(shamt), .result(rightshift_1_result));
  lessThan lessthan_1 (.A(inputData1), .B(inputData2), .result(smaller));
  isZero iszero_1 (.A(inputData1), .result(allZeroes));
  Multiplexer #(.select(4), .width(16), .enable("false")) multiplexer_1 (
    .in0(addandsub_1_result), .in1(addandsub_2_result), .in2(addandsub_3_result), .in3(not_1_out),
    .in4(xor_1_out), .in5(leftshift_1_result), .in6(rightshift_1_result), .in7(addandsub_1_result),
    .in8(addandsub_1_result), .out(outputData), .sel(opType));  // open: in9, in10, in11, in12, in13, in14, in15

  // Other names for the same wires on the sheet: A[15:0] = inputData1; B[15:0] = inputData2
endmodule

module fullAdder (
  input  A,
  input  B,
  input  Cin,
  output Sum,
  output Cout
);

  wire and_1_out, and_2_out, xor_1_out;

  xor xor_1 (xor_1_out, A, B);
  and and_1 (and_1_out, Cin, xor_1_out);
  and and_2 (and_2_out, A, B);
  xor xor_2 (Sum, xor_1_out, Cin);
  or or_1 (Cout, and_1_out, and_2_out);
endmodule

module addAndSub (
  input  sub,
  input  [15:0] A,
  input  [15:0] B,
  output [15:0] result,
  output ovf
);

  wire Cout0, Cout1, Cout2, Cout3, Cout4, Cout5, Cout6, Cout7, Cout8, Cout9, Cout10, Cout11, Cout12, Cout13,
       Cout14, Cout15, xor_1_out, xor_2_out, xor_3_out, xor_4_out, xor_5_out, xor_6_out, xor_7_out,
       xor_8_out, xor_9_out, xor_10_out, xor_11_out, xor_12_out, xor_13_out, xor_14_out, xor_15_out,
       xor_16_out, xor_17_out;

  xor xor_1 (xor_1_out, sub, B[0]);
  xor xor_2 (xor_2_out, sub, B[1]);
  xor xor_3 (xor_3_out, sub, B[2]);
  xor xor_4 (xor_4_out, sub, B[3]);
  xor xor_5 (xor_5_out, sub, B[4]);
  xor xor_6 (xor_6_out, sub, B[5]);
  xor xor_7 (xor_7_out, sub, B[6]);
  xor xor_8 (xor_8_out, sub, B[7]);
  xor xor_9 (xor_9_out, sub, B[8]);
  xor xor_10 (xor_10_out, sub, B[9]);
  xor xor_11 (xor_11_out, sub, B[10]);
  xor xor_12 (xor_12_out, sub, B[11]);
  xor xor_13 (xor_13_out, sub, B[12]);
  xor xor_14 (xor_14_out, sub, B[13]);
  xor xor_15 (xor_15_out, sub, B[14]);
  xor xor_16 (xor_16_out, sub, B[15]);
  fullAdder fulladder_1 (.A(A[0]), .B(xor_1_out), .Cin(sub), .Sum(result[0]), .Cout(Cout0));
  fullAdder fulladder_2 (.A(A[1]), .B(xor_2_out), .Cin(Cout0), .Sum(result[1]), .Cout(Cout1));
  fullAdder fulladder_3 (.A(A[2]), .B(xor_3_out), .Cin(Cout1), .Sum(result[2]), .Cout(Cout2));
  fullAdder fulladder_4 (.A(A[3]), .B(xor_4_out), .Cin(Cout2), .Sum(result[3]), .Cout(Cout3));
  fullAdder fulladder_5 (.A(A[4]), .B(xor_5_out), .Cin(Cout3), .Sum(result[4]), .Cout(Cout4));
  fullAdder fulladder_6 (.A(A[5]), .B(xor_6_out), .Cin(Cout4), .Sum(result[5]), .Cout(Cout5));
  fullAdder fulladder_7 (.A(A[6]), .B(xor_7_out), .Cin(Cout5), .Sum(result[6]), .Cout(Cout6));
  fullAdder fulladder_8 (.A(A[7]), .B(xor_8_out), .Cin(Cout6), .Sum(result[7]), .Cout(Cout7));
  fullAdder fulladder_9 (.A(A[8]), .B(xor_9_out), .Cin(Cout7), .Sum(result[8]), .Cout(Cout8));
  fullAdder fulladder_10 (.A(A[9]), .B(xor_10_out), .Cin(Cout8), .Sum(result[9]), .Cout(Cout9));
  fullAdder fulladder_11 (.A(A[10]), .B(xor_11_out), .Cin(Cout9), .Sum(result[10]), .Cout(Cout10));
  fullAdder fulladder_12 (.A(A[11]), .B(xor_12_out), .Cin(Cout10), .Sum(result[11]), .Cout(Cout11));
  fullAdder fulladder_13 (.A(A[12]), .B(xor_13_out), .Cin(Cout11), .Sum(result[12]), .Cout(Cout12));
  fullAdder fulladder_14 (.A(A[13]), .B(xor_14_out), .Cin(Cout12), .Sum(result[13]), .Cout(Cout13));
  fullAdder fulladder_15 (.A(A[14]), .B(xor_15_out), .Cin(Cout13), .Sum(result[14]), .Cout(Cout14));
  fullAdder fulladder_16 (.A(A[15]), .B(xor_16_out), .Cin(Cout14), .Sum(result[15]), .Cout(Cout15));
  xor xor_17 (xor_17_out, sub, B[0]);
  xor xor_18 (ovf, Cout14, Cout15);

  // Other names for the same wires on the sheet: r0 = result[0]; r1 = result[1]; r2 = result[2]; r3 = result[3];
  //   r4 = result[4]; r5 = result[5]; r6 = result[6]; r7 = result[7]; r8 = result[8]; r9 = result[9];
  //   r10 = result[10]; r11 = result[11]; r12 = result[12]; r13 = result[13]; r14 = result[14]; r15 = result[15]
endmodule

module PCReg (
  input  [15:0] dataIn,
  input  clk,
  input  reset,
  output [15:0] dataOut
);

  singleRegister singleregister_1 (.datain(dataIn), .clk(clk), .writeEnable(1'b1), .reset(reset), .dataOut(dataOut));
endmodule

module InstrucSplitter (
  input  [15:0] Instruction,
  output [5:0] imm,
  output [3:0] Opcode,
  output [2:0] rs,
  output [2:0] rt,
  output [2:0] rd,
  output [11:0] address,
  output [2:0] shamt
);


  assign address = Instruction[11:0];
  assign imm = Instruction[5:0];
  assign Opcode = Instruction[15:12];
  assign rd = Instruction[5:3];
  assign rs = Instruction[11:9];
  assign rt = Instruction[8:6];
  assign shamt = Instruction[2:0];

  // Other names for the same wires on the sheet: i0 = Instruction[0]; i1 = Instruction[1]; i2 = Instruction[2];
  //   i3 = Instruction[3]; i4 = Instruction[4]; i5 = Instruction[5]; i6 = Instruction[6]; i7 = Instruction[7];
  //   i8 = Instruction[8]; i9 = Instruction[9]; i10 = Instruction[10]; i11 = Instruction[11]; i12 = Instruction[12];
  //   i13 = Instruction[13]; i14 = Instruction[14]; i15 = Instruction[15]
endmodule

module isZero (
  input  [15:0] A,
  output result
);

  wire not_1_out, not_2_out, not_3_out, not_4_out, not_5_out, not_6_out, not_7_out, not_8_out, not_9_out,
       not_10_out, not_11_out, not_12_out, not_13_out, not_14_out, not_15_out, not_16_out;

  not not_1 (not_1_out, A[0]);
  not not_2 (not_2_out, A[1]);
  not not_3 (not_3_out, A[2]);
  not not_4 (not_4_out, A[3]);
  not not_5 (not_5_out, A[4]);
  not not_6 (not_6_out, A[5]);
  not not_7 (not_7_out, A[6]);
  not not_8 (not_8_out, A[7]);
  not not_9 (not_9_out, A[8]);
  not not_10 (not_10_out, A[9]);
  not not_11 (not_11_out, A[10]);
  not not_12 (not_12_out, A[11]);
  not not_13 (not_13_out, A[12]);
  not not_14 (not_14_out, A[13]);
  and and_1 (result, not_1_out, not_2_out, not_3_out, not_4_out, not_5_out, not_6_out, not_7_out, not_8_out, not_9_out, not_10_out, not_11_out, not_12_out, not_13_out, not_14_out, not_15_out, not_16_out);
  not not_15 (not_15_out, A[14]);
  not not_16 (not_16_out, A[15]);
endmodule

module leftShift (
  input  [15:0] A,
  input  [2:0] shamt,
  output [15:0] result
);

  wire i1_0, i1_1, i1_2, i1_3, i1_4, i1_5, i1_6, i1_7, i1_8, i1_9, i1_10, i1_11, i1_12, i1_13, i1_14, i1_15,
       i2_0, i2_1, i2_2, i2_3, i2_4, i2_5, i2_6, i2_7, i2_8, i2_9, i2_10, i2_11, i2_12, i2_13, i2_14, i2_15;

  Multiplexer #(.enable("false")) multiplexer_1 (.in0(A[15]), .in1(A[14]), .out(i1_15), .sel(shamt[0]));
  Multiplexer #(.enable("false")) multiplexer_2 (.in0(A[14]), .in1(A[13]), .out(i1_14), .sel(shamt[0]));
  Multiplexer #(.enable("false")) multiplexer_3 (.in0(A[13]), .in1(A[12]), .out(i1_13), .sel(shamt[0]));
  Multiplexer #(.enable("false")) multiplexer_4 (.in0(A[12]), .in1(A[11]), .out(i1_12), .sel(shamt[0]));
  Multiplexer #(.enable("false")) multiplexer_5 (.in0(A[11]), .in1(A[10]), .out(i1_11), .sel(shamt[0]));
  Multiplexer #(.enable("false")) multiplexer_6 (.in0(A[10]), .in1(A[9]), .out(i1_10), .sel(shamt[0]));
  Multiplexer #(.enable("false")) multiplexer_7 (.in0(A[9]), .in1(A[8]), .out(i1_9), .sel(shamt[0]));
  Multiplexer #(.enable("false")) multiplexer_8 (.in0(A[1]), .in1(A[0]), .out(i1_1), .sel(shamt[0]));
  Multiplexer #(.enable("false")) multiplexer_9 (.in0(A[8]), .in1(A[7]), .out(i1_8), .sel(shamt[0]));
  Multiplexer #(.enable("false")) multiplexer_10 (.in0(A[7]), .in1(A[6]), .out(i1_7), .sel(shamt[0]));
  Multiplexer #(.enable("false")) multiplexer_11 (.in0(A[6]), .in1(A[5]), .out(i1_6), .sel(shamt[0]));
  Multiplexer #(.enable("false")) multiplexer_12 (.in0(A[5]), .in1(A[4]), .out(i1_5), .sel(shamt[0]));
  Multiplexer #(.enable("false")) multiplexer_13 (.in0(A[4]), .in1(A[3]), .out(i1_4), .sel(shamt[0]));
  Multiplexer #(.enable("false")) multiplexer_14 (.in0(A[3]), .in1(A[2]), .out(i1_3), .sel(shamt[0]));
  Multiplexer #(.enable("false")) multiplexer_15 (.in0(A[2]), .in1(A[1]), .out(i1_2), .sel(shamt[0]));
  Multiplexer #(.enable("false")) multiplexer_16 (.in0(A[0]), .in1(1'b0), .out(i1_0), .sel(shamt[0]));
  Multiplexer #(.enable("false")) multiplexer_17 (.in0(i1_15), .in1(i1_13), .out(i2_15), .sel(shamt[1]));
  Multiplexer #(.enable("false")) multiplexer_18 (.in0(i1_14), .in1(i1_12), .out(i2_14), .sel(shamt[1]));
  Multiplexer #(.enable("false")) multiplexer_19 (.in0(i1_13), .in1(i1_11), .out(i2_13), .sel(shamt[1]));
  Multiplexer #(.enable("false")) multiplexer_20 (.in0(i1_12), .in1(i1_10), .out(i2_12), .sel(shamt[1]));
  Multiplexer #(.enable("false")) multiplexer_21 (.in0(i1_11), .in1(i1_9), .out(i2_11), .sel(shamt[1]));
  Multiplexer #(.enable("false")) multiplexer_22 (.in0(i1_10), .in1(i1_8), .out(i2_10), .sel(shamt[1]));
  Multiplexer #(.enable("false")) multiplexer_23 (.in0(i1_9), .in1(i1_7), .out(i2_9), .sel(shamt[1]));
  Multiplexer #(.enable("false")) multiplexer_24 (.in0(i1_1), .in1(1'b0), .out(i2_1), .sel(shamt[1]));
  Multiplexer #(.enable("false")) multiplexer_25 (.in0(i1_8), .in1(i1_6), .out(i2_8), .sel(shamt[1]));
  Multiplexer #(.enable("false")) multiplexer_26 (.in0(i1_7), .in1(i1_5), .out(i2_7), .sel(shamt[1]));
  Multiplexer #(.enable("false")) multiplexer_27 (.in0(i1_6), .in1(i1_4), .out(i2_6), .sel(shamt[1]));
  Multiplexer #(.enable("false")) multiplexer_28 (.in0(i1_5), .in1(i1_3), .out(i2_5), .sel(shamt[1]));
  Multiplexer #(.enable("false")) multiplexer_29 (.in0(i1_4), .in1(i1_2), .out(i2_4), .sel(shamt[1]));
  Multiplexer #(.enable("false")) multiplexer_30 (.in0(i1_3), .in1(i1_1), .out(i2_3), .sel(shamt[1]));
  Multiplexer #(.enable("false")) multiplexer_31 (.in0(i1_2), .in1(i1_0), .out(i2_2), .sel(shamt[1]));
  Multiplexer #(.enable("false")) multiplexer_32 (.in0(i1_0), .in1(1'b0), .out(i2_0), .sel(shamt[1]));
  Multiplexer #(.enable("false")) multiplexer_33 (.in0(i2_15), .in1(i2_11), .out(result[15]), .sel(shamt[2]));
  Multiplexer #(.enable("false")) multiplexer_34 (.in0(i2_14), .in1(i2_10), .out(result[14]), .sel(shamt[2]));
  Multiplexer #(.enable("false")) multiplexer_35 (.in0(i2_13), .in1(i2_9), .out(result[13]), .sel(shamt[2]));
  Multiplexer #(.enable("false")) multiplexer_36 (.in0(i2_12), .in1(i2_8), .out(result[12]), .sel(shamt[2]));
  Multiplexer #(.enable("false")) multiplexer_37 (.in0(i2_11), .in1(i2_7), .out(result[11]), .sel(shamt[2]));
  Multiplexer #(.enable("false")) multiplexer_38 (.in0(i2_10), .in1(i2_6), .out(result[10]), .sel(shamt[2]));
  Multiplexer #(.enable("false")) multiplexer_39 (.in0(i2_9), .in1(i2_5), .out(result[9]), .sel(shamt[2]));
  Multiplexer #(.enable("false")) multiplexer_40 (.in0(i2_1), .in1(1'b0), .out(result[1]), .sel(shamt[2]));
  Multiplexer #(.enable("false")) multiplexer_41 (.in0(i2_8), .in1(i2_4), .out(result[8]), .sel(shamt[2]));
  Multiplexer #(.enable("false")) multiplexer_42 (.in0(i2_7), .in1(i2_3), .out(result[7]), .sel(shamt[2]));
  Multiplexer #(.enable("false")) multiplexer_43 (.in0(i2_6), .in1(i2_2), .out(result[6]), .sel(shamt[2]));
  Multiplexer #(.enable("false")) multiplexer_44 (.in0(i2_5), .in1(i2_1), .out(result[5]), .sel(shamt[2]));
  Multiplexer #(.enable("false")) multiplexer_45 (.in0(i2_4), .in1(i2_0), .out(result[4]), .sel(shamt[2]));
  Multiplexer #(.enable("false")) multiplexer_46 (.in0(i2_3), .in1(1'b0), .out(result[3]), .sel(shamt[2]));
  Multiplexer #(.enable("false")) multiplexer_47 (.in0(i2_2), .in1(1'b0), .out(result[2]), .sel(shamt[2]));
  Multiplexer #(.enable("false")) multiplexer_48 (.in0(i2_0), .in1(1'b0), .out(result[0]), .sel(shamt[2]));

  // Other names for the same wires on the sheet: r0 = result[0]; r1 = result[1]; r2 = result[2]; r3 = result[3];
  //   r4 = result[4]; r5 = result[5]; r6 = result[6]; r7 = result[7]; r8 = result[8]; r9 = result[9];
  //   r10 = result[10]; r11 = result[11]; r12 = result[12]; r13 = result[13]; r14 = result[14]; r15 = result[15];
  //   s0 = shamt[0]; s1 = shamt[1]; s2 = shamt[2]
endmodule

module rightShift (
  input  [15:0] A,
  input  [2:0] shamt,
  output [15:0] result
);

  wire i1_0, i1_1, i1_2, i1_3, i1_4, i1_5, i1_6, i1_7, i1_8, i1_9, i1_10, i1_11, i1_12, i1_13, i1_14, i1_15,
       i2_0, i2_1, i2_2, i2_3, i2_4, i2_5, i2_6, i2_7, i2_8, i2_9, i2_10, i2_11, i2_12, i2_13, i2_14, i2_15;

  Multiplexer #(.enable("false")) multiplexer_1 (.in0(A[0]), .in1(A[1]), .out(i1_15), .sel(shamt[0]));
  Multiplexer #(.enable("false")) multiplexer_2 (.in0(A[1]), .in1(A[2]), .out(i1_14), .sel(shamt[0]));
  Multiplexer #(.enable("false")) multiplexer_3 (.in0(A[2]), .in1(A[3]), .out(i1_13), .sel(shamt[0]));
  Multiplexer #(.enable("false")) multiplexer_4 (.in0(A[3]), .in1(A[4]), .out(i1_12), .sel(shamt[0]));
  Multiplexer #(.enable("false")) multiplexer_5 (.in0(A[4]), .in1(A[5]), .out(i1_11), .sel(shamt[0]));
  Multiplexer #(.enable("false")) multiplexer_6 (.in0(A[5]), .in1(A[6]), .out(i1_10), .sel(shamt[0]));
  Multiplexer #(.enable("false")) multiplexer_7 (.in0(A[6]), .in1(A[7]), .out(i1_9), .sel(shamt[0]));
  Multiplexer #(.enable("false")) multiplexer_8 (.in0(A[14]), .in1(A[15]), .out(i1_1), .sel(shamt[0]));
  Multiplexer #(.enable("false")) multiplexer_9 (.in0(A[7]), .in1(A[8]), .out(i1_8), .sel(shamt[0]));
  Multiplexer #(.enable("false")) multiplexer_10 (.in0(A[8]), .in1(A[9]), .out(i1_7), .sel(shamt[0]));
  Multiplexer #(.enable("false")) multiplexer_11 (.in0(A[9]), .in1(A[10]), .out(i1_6), .sel(shamt[0]));
  Multiplexer #(.enable("false")) multiplexer_12 (.in0(A[10]), .in1(A[11]), .out(i1_5), .sel(shamt[0]));
  Multiplexer #(.enable("false")) multiplexer_13 (.in0(A[11]), .in1(A[12]), .out(i1_4), .sel(shamt[0]));
  Multiplexer #(.enable("false")) multiplexer_14 (.in0(A[12]), .in1(A[13]), .out(i1_3), .sel(shamt[0]));
  Multiplexer #(.enable("false")) multiplexer_15 (.in0(A[13]), .in1(A[14]), .out(i1_2), .sel(shamt[0]));
  Multiplexer #(.enable("false")) multiplexer_16 (.in0(A[15]), .in1(1'b0), .out(i1_0), .sel(shamt[0]));
  Multiplexer #(.enable("false")) multiplexer_17 (.in0(i1_15), .in1(i1_13), .out(i2_15), .sel(shamt[1]));
  Multiplexer #(.enable("false")) multiplexer_18 (.in0(i1_14), .in1(i1_12), .out(i2_14), .sel(shamt[1]));
  Multiplexer #(.enable("false")) multiplexer_19 (.in0(i1_13), .in1(i1_11), .out(i2_13), .sel(shamt[1]));
  Multiplexer #(.enable("false")) multiplexer_20 (.in0(i1_12), .in1(i1_10), .out(i2_12), .sel(shamt[1]));
  Multiplexer #(.enable("false")) multiplexer_21 (.in0(i1_11), .in1(i1_9), .out(i2_11), .sel(shamt[1]));
  Multiplexer #(.enable("false")) multiplexer_22 (.in0(i1_10), .in1(i1_8), .out(i2_10), .sel(shamt[1]));
  Multiplexer #(.enable("false")) multiplexer_23 (.in0(i1_9), .in1(i1_7), .out(i2_9), .sel(shamt[1]));
  Multiplexer #(.enable("false")) multiplexer_24 (.in0(i1_1), .in1(1'b0), .out(i2_1), .sel(shamt[1]));
  Multiplexer #(.enable("false")) multiplexer_25 (.in0(i1_8), .in1(i1_6), .out(i2_8), .sel(shamt[1]));
  Multiplexer #(.enable("false")) multiplexer_26 (.in0(i1_7), .in1(i1_5), .out(i2_7), .sel(shamt[1]));
  Multiplexer #(.enable("false")) multiplexer_27 (.in0(i1_6), .in1(i1_4), .out(i2_6), .sel(shamt[1]));
  Multiplexer #(.enable("false")) multiplexer_28 (.in0(i1_5), .in1(i1_3), .out(i2_5), .sel(shamt[1]));
  Multiplexer #(.enable("false")) multiplexer_29 (.in0(i1_4), .in1(i1_2), .out(i2_4), .sel(shamt[1]));
  Multiplexer #(.enable("false")) multiplexer_30 (.in0(i1_3), .in1(i1_1), .out(i2_3), .sel(shamt[1]));
  Multiplexer #(.enable("false")) multiplexer_31 (.in0(i1_2), .in1(i1_0), .out(i2_2), .sel(shamt[1]));
  Multiplexer #(.enable("false")) multiplexer_32 (.in0(i1_0), .in1(1'b0), .out(i2_0), .sel(shamt[1]));
  Multiplexer #(.enable("false")) multiplexer_33 (.in0(i2_15), .in1(i2_11), .out(result[0]), .sel(shamt[2]));
  Multiplexer #(.enable("false")) multiplexer_34 (.in0(i2_14), .in1(i2_10), .out(result[1]), .sel(shamt[2]));
  Multiplexer #(.enable("false")) multiplexer_35 (.in0(i2_13), .in1(i2_9), .out(result[2]), .sel(shamt[2]));
  Multiplexer #(.enable("false")) multiplexer_36 (.in0(i2_12), .in1(i2_8), .out(result[3]), .sel(shamt[2]));
  Multiplexer #(.enable("false")) multiplexer_37 (.in0(i2_11), .in1(i2_7), .out(result[4]), .sel(shamt[2]));
  Multiplexer #(.enable("false")) multiplexer_38 (.in0(i2_10), .in1(i2_6), .out(result[5]), .sel(shamt[2]));
  Multiplexer #(.enable("false")) multiplexer_39 (.in0(i2_9), .in1(i2_5), .out(result[6]), .sel(shamt[2]));
  Multiplexer #(.enable("false")) multiplexer_40 (.in0(i2_1), .in1(1'b0), .out(result[14]), .sel(shamt[2]));
  Multiplexer #(.enable("false")) multiplexer_41 (.in0(i2_8), .in1(i2_4), .out(result[7]), .sel(shamt[2]));
  Multiplexer #(.enable("false")) multiplexer_42 (.in0(i2_7), .in1(i2_3), .out(result[8]), .sel(shamt[2]));
  Multiplexer #(.enable("false")) multiplexer_43 (.in0(i2_6), .in1(i2_2), .out(result[9]), .sel(shamt[2]));
  Multiplexer #(.enable("false")) multiplexer_44 (.in0(i2_5), .in1(i2_1), .out(result[10]), .sel(shamt[2]));
  Multiplexer #(.enable("false")) multiplexer_45 (.in0(i2_4), .in1(i2_0), .out(result[11]), .sel(shamt[2]));
  Multiplexer #(.enable("false")) multiplexer_46 (.in0(i2_3), .in1(1'b0), .out(result[12]), .sel(shamt[2]));
  Multiplexer #(.enable("false")) multiplexer_47 (.in0(i2_2), .in1(1'b0), .out(result[13]), .sel(shamt[2]));
  Multiplexer #(.enable("false")) multiplexer_48 (.in0(i2_0), .in1(1'b0), .out(result[15]), .sel(shamt[2]));

  // Other names for the same wires on the sheet: r15 = result[0]; r14 = result[1]; r13 = result[2]; r12 = result[3];
  //   r11 = result[4]; r10 = result[5]; r9 = result[6]; r8 = result[7]; r7 = result[8]; r6 = result[9];
  //   r5 = result[10]; r4 = result[11]; r3 = result[12]; r2 = result[13]; r1 = result[14]; r0 = result[15];
  //   s0 = shamt[0]; s1 = shamt[1]; s2 = shamt[2]
endmodule

module lessThan (
  input  [15:0] A,
  input  [15:0] B,
  output result
);

  wire [14:0] addandsub_1_result;

  addAndSub addandsub_1 (.sub(1'b1), .A(A), .B(B), .result({result, addandsub_1_result}));  // open: ovf
endmodule

module memory_latch (
  input  [15:0] address,
  input  WE,
  input  clk,
  input  [15:0] data_in,
  output [15:0] address_latched,
  output WE_latched,
  output OE_latched,
  output [15:0] data_in_latched
);

  wire DMwe_latch_q;
  wire [15:0] addr_latch_q;

  Register #(.width(16), .trigger("falling")) addr_latch (
    .D(address), .en(WE), .clk(clk), .Q(addr_latch_q));  // open: clr
  D_Flip_Flop #(.trigger("falling")) DMwe_latch (.D(WE), .clk(clk), .Q(DMwe_latch_q));  // open: Qn, preset, reset
  Register #(.width(16), .trigger("falling")) data_to_be_written (
    .D(data_in), .en(WE), .clk(clk), .Q(data_in_latched));  // open: clr
  Multiplexer #(.width(16), .enable("false")) multiplexer_1 (
    .in0(address), .in1(addr_latch_q), .out(address_latched), .sel(DMwe_latch_q));
  and and_1 (WE_latched, clk, DMwe_latch_q);
  not not_1 (OE_latched, WE_latched);
endmodule
